# Fritzing sketch Diagram (saved by Fritzing 0.9.3b)
breadboards: 1

parts:
  Part1 = Arduino Uno (Rev3)
  T1 = TMP36 Temperature Sensor [package="TO92 [THT]"]
  J1 = Piezo Speaker
  S1 = Pushbutton [package="[SMD]"]
  R2 = Resistor [tolerance=±5% resistance=10k package=THT]

nets:
  N1: Part1.A0, T1.Vout
  N2: Part1.D2, S1.Pin_1, S1.Pin_2, R2.Pin_0
  N3: Part1.D3_PWM, J1.pin2
  N4: Part1.ioref, T1.GND, J1.pin1, R2.Pin_1
  N5: Part1.N/C, T1.+Vs, S1.Pin_3, S1.Pin_4
